# Fritzing sketch MaP-Color-Sensor-Protoboard (saved by Fritzing 0.9.3b)
stripboards: 2

parts:
  R4 = Photocell (LDR) [package=THT]
  R1 = Resistor [tolerance=±5% resistance=150 package=THT]
  R2 = Resistor [tolerance=±5% resistance=150 package=THT]
  R3 = Resistor [tolerance=±5% resistance=150 package=THT]
  LED1 = RGB LED (com. cathode, rbg) [package="5 mm [THT]"]
  Part1 = Arduino Sensor Shield v5.0
  J1 = female pin header, 5 pins [form="♀ (female)"]

nets:
  GND: R4.pin_0, LED1.common_cathode, Part1.GND, J1.pin2
  N1: R4.pin_1, Part1.A0, Part1.D0, J1.pin5
  N2: R1.Pin_0, Part1.D11, J1.pin4
  N3: R1.Pin_1, LED1.green_anode
  N4: R2.Pin_0, Part1.D10, J1.pin3
  N5: R2.Pin_1, LED1.blue_anode
  N6: R3.Pin_0, Part1.D9, J1.pin1
  N7: R3.Pin_1, LED1.red_anode

notes:
  Front
  Back
