# Fritzing sketch MaP-Color-Sensor (saved by Fritzing 0.9.3b)
breadboards: 1

parts:
  Part1 = Arduino Sensor Shield v5.0
  R1 = Resistor [tolerance=±5% resistance=150 package=THT]
  R2 = Resistor [tolerance=±5% resistance=150 package=THT]
  R3 = Resistor [tolerance=±5% resistance=150 package=THT]
  LED1 = RGB LED (com. cathode, rbg) [package="5 mm [THT]"]
  R4 = Photocell (LDR) [package=THT]

nets:
  N1: Part1.A0, R4.pin_1
  N2: Part1.GND, LED1.common_cathode, R4.pin_0
  N3: Part1.D9, R1.Pin_0
  N4: Part1.D10, R3.Pin_0
  N5: Part1.D11, R2.Pin_0
  N6: R1.Pin_1, LED1.red_anode
  N7: R2.Pin_1, LED1.blue_anode
  N8: R3.Pin_1, LED1.green_anode
