# Fritzing sketch MaP-IR-Distance-Sensor (saved by Fritzing 0.9.3b)
breadboards: 1

parts:
  Part1 = Arduino Sensor Shield v5.0
  J1 = Infrared Proximity Sensor [part_number=GP2Y0A41SK0F]

nets:
  N1: Part1.A1, J1.Vout
  GND: Part1.GND, J1.GND
  +5V: Part1.+5V, J1.Vcc
