# Fritzing sketch MaP-PIR-Sensor (saved by Fritzing 0.9.3b)
breadboards: 1

parts:
  Part1 = Arduino Sensor Shield v5.0
  PIR1 = PIR sensor
  R1 = Resistor [tolerance=±5% resistance=1.5k package=THT]
  LED1 = LED - 5mm [color="Red (633nm)" package="5 mm [THT]"]

nets:
  N1: Part1.D2, PIR1.SIG, R1.Pin_0
  +5V: Part1.+5V, PIR1.VDD
  GND: Part1.GND, PIR1.GND, LED1.cathode
  N2: R1.Pin_1, LED1.anode
