# Fritzing sketch MaP-Status-LED-Set (saved by Fritzing 0.9.3b)
breadboards: 1

parts:
  Part1 = Arduino Sensor Shield v5.0
  R1 = Resistor [tolerance=±5% resistance=150 package=THT]
  R2 = Resistor [tolerance=±5% resistance=150 package=THT]
  R3 = Resistor [tolerance=±5% resistance=150 package=THT]
  LED1 = LED - 5mm [color="Red (633nm)" package="5 mm [THT]"]
  LED2 = LED - 5mm [color="Green (555nm)" package="5 mm [THT]"]
  LED3 = LED - 5mm [color="Blue (430nm)" package="5 mm [THT]"]

nets:
  N1: Part1.GND, R1.Pin_0, R2.Pin_0, R3.Pin_0
  N2: Part1.D9, LED1.anode
  N3: Part1.D10, LED2.anode
  N4: Part1.D11, LED3.anode
  N5: R1.Pin_1, LED3.cathode
  N6: R2.Pin_1, LED1.cathode
  N7: R3.Pin_1, LED2.cathode
