# Fritzing sketch MaP-Status-LED (saved by Fritzing 0.9.3b)
breadboards: 1

parts:
  Part1 = Arduino Sensor Shield v5.0
  R1 = Resistor [tolerance=±5% resistance=150 package=THT]
  R2 = Resistor [tolerance=±5% resistance=150 package=THT]
  R3 = Resistor [tolerance=±5% resistance=150 package=THT]
  LED1 = RGB LED (com. cathode, rbg) [package="5 mm [THT]"]

nets:
  N1: Part1.D9, R1.Pin_0
  N2: Part1.D10, R3.Pin_0
  N3: Part1.D11, R2.Pin_0
  N4: R1.Pin_1, LED1.red_anode
  N5: R2.Pin_1, LED1.blue_anode
  N6: R3.Pin_1, LED1.green_anode
